# Fritzing sketch daisychain_hub --pi (saved by Fritzing 0.9.3b)
circuit board: 3.05cm x 6.57cm
breadboards: 1

parts:
  SparkFun_74HC4051_8-Channel_Mux_Breakout2 = SparkFun-74HC4051-8-Channel-Mux-Breakout [part_number=BOB-13906]  # not connected
  J5 = female pin header, 6 pins [form="♀ (female)"]
  MCU1 = Raspberry Pi Zero  # not connected
  J6 = double row female pin header, 40 pins [form="♀ (female)"]
  J8 = female pin header, 11 pins [form="♀ (female)"]
  J7 = female pin header, 8 pins [form="♀ (female)"]

nets:
  N1: J5.pin2, J6.pin21, J8.pin2, J7.pin2
  N2: J5.pin3, J8.pin6
  N3: J5.pin4, J8.pin5
  N4: J5.pin5, J8.pin4
  N5: J5.pin6, J6.pin23
  N6: J6.pin12, J7.pin7
  N7: J6.pin13, J7.pin6
  N8: J6.pin22, J7.pin4
  N9: J6.pin28, J7.pin5

notes:
  SCL
  SDA0
  SDA1
  SDA2
  SDA
  23
  S1
  22
  24
  S2
  S0
  Z
  3.3V
  VCC
  GND
  LOCAR Pi Wing v.1.0
