# Fritzing sketch daisychain_hub --xs (saved by Fritzing 0.9.3b)
circuit board: 2.33592cm x 5.11714cm
circuit board: 2.33592cm x 5.11714cm
breadboards: 1

parts:
  SparkFun_74HC4051_8-Channel_Mux_Breakout1 = SparkFun-74HC4051-8-Channel-Mux-Breakout [part_number=BOB-13906]
  Part1 = Adafruit HUZZAH32 ESP32 Feather [part_number="Adafruit #3405"]  # not connected
  J1 = Generic female header - 6 pins [form="♀ (female)" package=THT]
  J2 = female pin header, 12 pins [form="♀ (female)"]  # not connected
  J3 = female pin header, 16 pins [form="♀ (female)"]
  J4 = Generic female header - 6 pins [form="♀ (female)" package=THT]
  SparkFun_74HC4051_8-Channel_Mux_Breakout2 = SparkFun-74HC4051-8-Channel-Mux-Breakout [part_number=BOB-13906]

nets:
  N1: SparkFun_74HC4051_8-Channel_Mux_Breakout1.VCC, J1.pin2
  N2: J3.pin15, J4.pin2, SparkFun_74HC4051_8-Channel_Mux_Breakout2.VCC

notes:
  GND
  VBATT
  3.3V

custom parts:
  Generic female header - 6 pins: Generic female header
