# Fritzing sketch psupply --v1 (saved by Fritzing 0.9.3b)
circuit board: 3.02814cm x 5.27166cm
breadboards: 1

parts:
  J1 = ATX24 Pin Power Supply Connector [package=atx24_right_angle]
  J2 = female pin header, 5 pins [form="♀ (female)"]
  J3 = female pin header, 5 pins [form="♀ (female)"]
  J4 = female pin header, 5 pins [form="♀ (female)"]
  J5 = female pin header, 5 pins [form="♀ (female)"]
  J6 = female pin header, 5 pins [form="♀ (female)"]
  J7 = female pin header, 5 pins [form="♀ (female)"]
  J8 = double row female pin header, 24 pins [form="♀ (female)"]

nets:
  N1: J1.3.3V, J2.pin1, J2.pin2, J2.pin3, J2.pin4, J2.pin5, J8.pin1, J8.pin2, J8.pin3, J8.pin22, J8.pin23, J8.pin24
  N2: J1.5V, J4.pin1, J4.pin2, J4.pin3, J4.pin4, J4.pin5, J8.pin4, J8.pin5, J8.pin6, J8.pin19, J8.pin20, J8.pin21
  N3: J1.PWR_OK, J8.pin15
  N4: J1.5V_STDBY, J8.pin11, J8.pin12, J8.pin13, J8.pin14
  N5: J1.12V, J6.pin1, J6.pin2, J6.pin3, J6.pin4, J6.pin5, J8.pin7, J8.pin8, J8.pin9, J8.pin16, J8.pin17, J8.pin18
  N6: J1.NC, J8.pin10
  N7: J3.pin1, J3.pin2, J3.pin3, J3.pin4, J3.pin5
  N8: J5.pin1, J5.pin2, J5.pin3, J5.pin4, J5.pin5
  N9: J7.pin1, J7.pin2, J7.pin3, J7.pin4, J7.pin5

notes:
  3.3v
  12v
  5v
  PWR_OK
  5v_SB
  NC
  GND
